# Fritzing sketch board-H12 (saved by Fritzing 1.0.8)
breadboards: 1

parts:
  Q6 = NPN-Transistor [package="TO92 [THT]"]
  Q7 = NPN-Transistor [package="TO92 [THT]"]
  Q8 = PNP-Transistor [package="TO92 [THT]"]
  Q9 = PNP-Transistor [package="TO92 [THT]"]
  R9 = Resistor [tolerance=±5% power=0.25W resistance=10k package=THT]
  R2 = Resistor [tolerance=±5% power=0.25W resistance=10k package=THT]
  R8 = Resistor [tolerance=±5% power=0.25W resistance=22k package=THT]
  R1 = Resistor [tolerance=±5% power=0.25W resistance=22k package=THT]
  R5 = Resistor [tolerance=±5% power=0.25W resistance=2.2k package=THT]
  R12 = Resistor [tolerance=±5% power=0.25W resistance=2.2k package=THT]
  R13 = Resistor [tolerance=±5% power=0.25W resistance=33k package=THT]
  R6 = Resistor [tolerance=±5% power=0.25W resistance=33k package=THT]
  R7 = Resistor [tolerance=±5% power=0.25W resistance=47k package=THT]
  R14 = Resistor [tolerance=±5% power=0.25W resistance=47k package=THT]
  R11 = Resistor [tolerance=±5% power=0.25W resistance=10k package=THT]
  R4 = Resistor [tolerance=±5% power=0.25W resistance=10k package=THT]
  R10 = Resistor [tolerance=±5% power=0.25W resistance=4.7k package=THT]
  R3 = Resistor [tolerance=±5% power=0.25W resistance=4.7k package=THT]
  Part3 = TRRS 3.5mm Jack Breakout
  JP4 = Header 4 [package=molex-1x4_lock]
  R15 = Resistor [tolerance=±5% power=0.25W resistance=100k package=THT]
  Q10 = 2N7000 FET N-Channel [part_number=2N7000 package=TO92]
  R16 = Resistor [tolerance=±5% power=0.25W resistance=1m package=THT]
  LED2 = LED - 5mm [color="Red (633nm)" current=0.030A package="5 mm [THT]"]
  R17 = Resistor [tolerance=±5% power=0.25W resistance=2.2k package=THT]
  C1 = Ceramic Capacitor [capacitance=100nF voltage=35V package="100 mil [THT, multilayer]"]

nets:
  N1: Q6.E, Q7.E, R8.Pin_1, R1.Pin_1, R7.Pin_0, R14.Pin_0, Part3.SLEEVE, Q10.source, R16.Pin_1, C1.1
  N2: Q6.B, R9.Pin_0
  N3: Q6.C, R10.Pin_1
  N4: Q7.B, R2.Pin_0
  N5: Q7.C, R3.Pin_1
  N6: Q8.E, Q9.E, R11.Pin_1, R4.Pin_1, R17.Pin_0, C1.0
  N7: Q8.B, R4.Pin_0, R3.Pin_0
  N8: Q8.C, R5.Pin_0
  N9: Q9.B, R11.Pin_0, R10.Pin_0
  N10: Q9.C, R12.Pin_0
  N11: R9.Pin_1, R8.Pin_0, JP4.4
  N12: R2.Pin_1, R1.Pin_0, JP4.2
  N13: R5.Pin_1, R6.Pin_0, Part3.RING1
  N14: R12.Pin_1, R13.Pin_0, Part3.TIP, R15.Pin_0
  N15: R13.Pin_1, R14.Pin_1, JP4.3
  N16: R6.Pin_1, R7.Pin_1, JP4.1
  N17: R15.Pin_1, Q10.gate, R16.Pin_0
  N18: Q10.drain, LED2.cathode
  N19: LED2.anode, R17.Pin_1

custom parts:
  2N7000 FET N-Channel: A 2N7000 MOSFET N-Channel Transistor
